# Fritzing sketch Signal_Circuit (saved by Fritzing 0.9.3b)
circuit board: 10cm x 6cm
breadboards: 1

parts:
  U1 = RELAY [package=relay-jzc]
  U2 = RELAY [package=relay-jzc]
  U3 = RELAY [package=relay-jzc]
  U4 = RELAY [package=relay-jzc]
  Q1 = NPN-Transistor [package="SOT-23 [SMD]"]
  Q2 = NPN-Transistor [package="SOT-23 [SMD]"]
  Q3 = NPN-Transistor [package="SOT-23 [SMD]"]
  Q4 = NPN-Transistor [package="SOT-23 [SMD]"]
  R1 = Resistor [tolerance=±5% resistance=220 package=THT]
  R2 = Resistor [tolerance=±5% resistance=220 package=THT]
  R3 = Resistor [tolerance=±5% resistance=220 package=THT]
  R4 = Resistor [tolerance=±5% resistance=220 package=THT]
  D5 = Rectifier Diode [part_number=1N4001 package="Melf DO-213 AB [SMD]"]
  D6 = Rectifier Diode [part_number=1N4001 package="Melf DO-213 AB [SMD]"]
  D7 = Rectifier Diode [part_number=1N4001 package="Melf DO-213 AB [SMD]"]
  D8 = Rectifier Diode [part_number=1N4001 package="Melf DO-213 AB [SMD]"]
  Input_1 = Audio Jack (TRRS) 3.5mm [part_number=Jack package="RC-5325A [SMD]"]
  Input_2 = Audio Jack (TRRS) 3.5mm [part_number=Jack package="RC-5325A [SMD]"]
  Input_3 = Audio Jack (TRRS) 3.5mm [part_number=Jack package="RC-5325A [SMD]"]
  Input_4 = Audio Jack (TRRS) 3.5mm [part_number=Jack package="RC-5325A [SMD]"]
  OUTPUT = Audio Jack (TRRS) 3.5mm [part_number=Jack package="RC-5325A [SMD]"]

nets:
  GND: U1.COIL2, U2.COIL2, U3.COIL2, U4.COIL2
  Signal 1: U1.NC, D5.anode
  Output: U1.NO, U2.NO, U3.NO, U4.NO, OUTPUT.SLEEVE
  N1: U1.MAIN, D5.cathode
  N2: U1.COIL1, Q1.2
  Signal 2: U2.NC, D6.anode
  N3: U2.MAIN, D6.cathode
  N4: U2.COIL1, Q2.2
  Signal 3: U3.NC, D7.anode
  N5: U3.MAIN, D7.cathode
  N6: U3.COIL1, Q3.2
  Signal 4: U4.NC, D8.anode
  N7: U4.MAIN, D8.cathode
  N8: U4.COIL1, Q4.2
  N9: Q1.0, R1.Pin_1
  5V: Q1.1, Q2.1, Q3.1, Q4.1
  N10: Q2.0, R2.Pin_1
  N11: Q3.0, R3.Pin_1
  N12: Q4.0, R4.Pin_1
  cSignalOne: R1.Pin_0
  cSignalTwo: R2.Pin_0
  cSignalThree: R3.Pin_0
  cSignalFor: R4.Pin_0
  Tip 1/Tip 4: Input_1.TIP, Input_4.TIP, OUTPUT.TIP
  Ring 1.1/Ring 1.2/Ring 1.3/Ring 1.4: Input_1.RING1, Input_2.RING1, Input_3.RING1, Input_4.RING1, OUTPUT.RING1
  Ring 2.1/Ring 2.3/Ring 2.4: Input_1.RING2, Input_3.RING2, Input_4.RING2, OUTPUT.RING2
  Tip 2: Input_2.TIP
  Ring 2.2: Input_2.RING2
  Tip 3: Input_3.TIP
